// Logisim project HRM_CPU.circ as structural Verilog: 8 circuits, main circuit main
module main (
);

  wire alu_1_negative, alu_1_overflow, alu_1_zero, clock_1_out, ctrl_1_eret, ctrl_1_mem_write, ctrl_1_mfc0,
       ctrl_1_mtc0, ctrl_1_reg_write, dm_1_wrong_addr, im_1_wrong_pc;
  wire [2:0] ctrl_1_npc_sel;
  wire [3:0] ctrl_1_alu_op;
  wire [4:0] im_1_op_code;
  wire [10:0] im_1_imm;
  wire [15:0] alu_1_write_data, cp0_1_cp0_pc, cp0_1_cp0_reg_value, dm_1_mem_value, multiplexer_1_out,
       npc_1_npc, PC_q, REG_q;

  Clock clock_1 (.out(clock_1_out));
  NPC npc_1 (
    .npc_sel(ctrl_1_npc_sel), .zero(alu_1_zero), .negative(alu_1_negative), .pc(PC_q), .npc(npc_1_npc),
    .imm(im_1_imm), .cp0_pc(cp0_1_cp0_pc));
  Register #(.width(16)) PC (.D(npc_1_npc), .Q(PC_q), .clk(clock_1_out));  // open: en, clr
  IM im_1 (.PC(PC_q), .op_code(im_1_op_code), .imm(im_1_imm), .wrong_pc(im_1_wrong_pc));
  Register #(.width(16)) REG (.D(multiplexer_1_out), .en(ctrl_1_reg_write), .Q(REG_q), .clk(clock_1_out));  // open: clr
  CTRL ctrl_1 (
    .npc_sel(ctrl_1_npc_sel), .alu_op(ctrl_1_alu_op), .mem_write(ctrl_1_mem_write),
    .reg_write(ctrl_1_reg_write), .eret(ctrl_1_eret), .mfc0(ctrl_1_mfc0), .mtc0(ctrl_1_mtc0),
    .in_1(im_1_op_code));
  DM dm_1 (
    .imm_value(im_1_imm), .reg_value(REG_q), .mem_write(ctrl_1_mem_write), .wrong_addr(dm_1_wrong_addr),
    .mem_value(dm_1_mem_value), .clk(clock_1_out));
  ALU alu_1 (
    .mem_value(dm_1_mem_value), .reg_value(REG_q), .imm(im_1_imm), .zero(alu_1_zero),
    .negative(alu_1_negative), .write_data(alu_1_write_data), .overflow(alu_1_overflow),
    .alu_op(ctrl_1_alu_op));
  CP0 cp0_1 (
    .overflow(alu_1_overflow), .wrong_pc(im_1_wrong_pc), .wrong_addr(dm_1_wrong_addr), .epc(PC_q),
    .cp0_pc(cp0_1_cp0_pc), .eret(ctrl_1_eret), .clk(clock_1_out), .cp0_write(ctrl_1_mtc0),
    .cp0_write_data(REG_q), .cp0_reg(im_1_imm), .cp0_reg_value(cp0_1_cp0_reg_value));
  Multiplexer #(.width(16)) multiplexer_1 (
    .in0(alu_1_write_data), .in1(cp0_1_cp0_reg_value), .out(multiplexer_1_out), .sel(ctrl_1_mfc0));  // open: en
endmodule

module NPC (
  input  [2:0] npc_sel,
  input  zero,
  input  negative,
  input  [15:0] pc,
  input  [10:0] imm,
  input  [15:0] cp0_pc,
  output [15:0] npc
);

  wire comparator_1_eq;
  wire [2:0] jump_1_npc_control0;
  wire [15:0] adder_1_out, bit_extender_1_out, multiplexer_1_out;

  Adder #(.width(16)) adder_1 (.a(pc), .b(16'h2), .out(adder_1_out));  // open: cin, cout
  assign bit_extender_1_out = {{5{1'b0}}, imm};  // Bit_Extender bit_extender_1
  JUMP jump_1 (
    .npc_sel2(npc_sel[2]), .npc_sel1(npc_sel[1]), .npc_sel0(npc_sel[0]), .zero(zero), .negative(negative),
    .npc_control2(jump_1_npc_control0[2]), .npc_control1(jump_1_npc_control0[1]),
    .npc_control0(jump_1_npc_control0[0]));
  Multiplexer #(.select(3), .width(16)) multiplexer_1 (
    .in0(adder_1_out), .in1(bit_extender_1_out), .in2(bit_extender_1_out), .in3(bit_extender_1_out),
    .out(multiplexer_1_out), .sel(jump_1_npc_control0));  // open: in4, in5, in6, in7, en
  Comparator #(.width(16)) comparator_1 (.a({16{1'b0}}), .b(cp0_pc), .eq(comparator_1_eq));  // open: gt, lt
  Multiplexer #(.width(16)) multiplexer_2 (
    .in0(cp0_pc), .in1(multiplexer_1_out), .out(npc), .sel(comparator_1_eq));  // open: en
endmodule

module JUMP (
  input  npc_sel2,
  input  npc_sel1,
  input  npc_sel0,
  input  zero,
  input  negative,
  output npc_control2,
  output npc_control1,
  output npc_control0
);

  wire and_1_out, and_2_out, and_3_out, and_4_out, not_1_out, not_2_out;

  not not_1 (not_1_out, npc_sel0);
  not not_2 (not_2_out, npc_sel1);
  and and_1 (and_1_out, npc_sel1, not_1_out, zero);
  or or_1 (npc_control1, and_1_out, and_2_out);
  and and_2 (and_2_out, npc_sel1, npc_sel0, negative);
  and and_3 (and_3_out, not_2_out, npc_sel0);
  or or_2 (npc_control0, and_3_out, and_4_out);
  and and_4 (and_4_out, npc_sel0, negative);

  assign npc_control2 = npc_sel2;
endmodule

module IM (
  input  [15:0] PC,
  output wrong_pc,
  output [4:0] op_code,
  output [10:0] imm
);

  ROM #(.addrWidth(16), .dataWidth(16)) rom_1 (.addr(PC), .data({imm, op_code}));  // open: sel
  Comparator #(.width(16)) comparator_1 (.a(PC), .b(16'h5000), .gt(wrong_pc));  // open: eq, lt
endmodule

module DM (
  input  [10:0] imm_value,
  input  [15:0] reg_value,
  input  mem_write,
  input  clk,
  output wrong_addr,
  output [15:0] mem_value
);

  Comparator #(.width(11)) comparator_1 (.a(imm_value), .b(11'h100), .gt(wrong_addr));  // open: eq, lt
  RAM #(.addrWidth(11), .dataWidth(16), .bus("separate")) ram_1 (
    .addr(imm_value), .din(reg_value), .data(mem_value), .str(mem_write), .clk(clk));  // open: sel, ld, clr
endmodule

module ALU (
  input  [15:0] mem_value,
  input  [15:0] reg_value,
  input  [10:0] imm,
  input  [3:0] alu_op,
  output zero,
  output negative,
  output [15:0] write_data,
  output overflow
);

  wire adder_1_cout, adder_2_cout, adder_3_cout, subtractor_1_bout, subtractor_2_bout, subtractor_3_bout;
  wire [15:0] adder_1_out, adder_2_out, adder_3_out, bit_extender_1_out, subtractor_1_out, subtractor_2_out,
       subtractor_3_out;

  assign bit_extender_1_out = {{5{1'b0}}, imm};  // Bit_Extender bit_extender_1
  Adder #(.width(16)) adder_1 (.a(mem_value), .b(reg_value), .out(adder_1_out), .cout(adder_1_cout));  // open: cin
  Subtractor #(.width(16)) subtractor_1 (
    .a(reg_value), .b(mem_value), .out(subtractor_1_out), .bout(subtractor_1_bout));  // open: bin
  Adder #(.width(16)) adder_2 (
    .a(reg_value), .b(bit_extender_1_out), .out(adder_2_out), .cout(adder_2_cout));  // open: cin
  Subtractor #(.width(16)) subtractor_2 (
    .a(reg_value), .b(bit_extender_1_out), .out(subtractor_2_out), .bout(subtractor_2_bout));  // open: bin
  Adder #(.width(16)) adder_3 (.a(mem_value), .b(16'h1), .out(adder_3_out), .cout(adder_3_cout));  // open: cin
  Subtractor #(.width(16)) subtractor_3 (
    .a(mem_value), .b(16'h1), .out(subtractor_3_out), .bout(subtractor_3_bout));  // open: bin
  Multiplexer #(.select(4), .width(16)) multiplexer_1 (
    .in0(adder_1_out), .in1(subtractor_1_out), .in2(adder_2_out), .in3(subtractor_2_out), .in4(adder_3_out),
    .in5(subtractor_3_out), .in6(mem_value), .in7(bit_extender_1_out), .out(write_data), .sel(alu_op));  // open: in8, in9, in10, in11, in12, in13, in14, in15, en
  Comparator #(.width(16)) comparator_1 (.a(reg_value), .b({16{1'b0}}), .eq(zero), .lt(negative));  // open: gt
  Multiplexer #(.select(4)) multiplexer_2 (
    .in0(adder_1_cout), .in1(subtractor_1_bout), .in2(adder_2_cout), .in3(subtractor_2_bout),
    .in4(adder_3_cout), .in5(subtractor_3_bout), .in6(1'b0), .in7(1'b0), .out(overflow), .sel(alu_op));  // open: in8, in9, in10, in11, in12, in13, in14, in15, en
endmodule

module CP0 (
  input  overflow,
  input  wrong_pc,
  input  wrong_addr,
  input  cp0_write,
  input  [15:0] epc,
  input  [10:0] cp0_reg,
  input  clk,
  input  eret,
  input  [15:0] cp0_write_data,
  output [15:0] cp0_reg_value,
  output [15:0] cp0_pc
);

  wire and_1_out, and_2_out, comparator_1_eq, comparator_2_eq, or_1_out, or_2_out;
  wire [1:0] bit_extender_1_out;
  wire [15:0] Cause_q, EPC_q, multiplexer_1_out, multiplexer_2_out, multiplexer_3_out, multiplexer_4_out,
       multiplexer_5_out, multiplexer_6_out;

  Comparator #(.width(2)) comparator_1 (.a(bit_extender_1_out), .b(2'b10), .eq(comparator_1_eq));  // open: gt, lt
  Comparator #(.width(2)) comparator_2 (.a(bit_extender_1_out), .b(2'b01), .eq(comparator_2_eq));  // open: gt, lt
  Bit_Extender #(.in_width(11), .out_width(2)) bit_extender_1 (.in(cp0_reg), .out(bit_extender_1_out));
  and and_1 (and_1_out, cp0_write, comparator_1_eq);
  Multiplexer #(.width(16)) multiplexer_1 (
    .in0({16{1'b0}}), .in1(16'h1), .out(multiplexer_1_out), .sel(overflow));  // open: en
  and and_2 (and_2_out, comparator_2_eq, cp0_write);
  Multiplexer #(.width(16)) multiplexer_2 (
    .in0(multiplexer_1_out), .in1(16'h2), .out(multiplexer_2_out), .sel(wrong_addr));  // open: en
  or or_1 (or_1_out, and_2_out, or_2_out);
  Multiplexer #(.width(16)) multiplexer_3 (
    .in0(cp0_write_data), .in1(epc), .out(multiplexer_3_out), .sel(or_2_out));  // open: en
  Multiplexer #(.width(16)) multiplexer_4 (
    .in0(multiplexer_2_out), .in1(16'h3), .out(multiplexer_4_out), .sel(wrong_pc));  // open: en
  Register #(.width(16)) u_EPC (.D(multiplexer_3_out), .en(or_1_out), .Q(EPC_q), .clk(clk));  // open: clr
  or or_2 (or_2_out, overflow, wrong_pc, wrong_addr);
  Multiplexer #(.width(16)) multiplexer_5 (
    .in0(cp0_write_data), .in1(multiplexer_4_out), .out(multiplexer_5_out), .sel(or_2_out));  // open: en
  Register #(.width(16)) Cause (.D(multiplexer_5_out), .en(and_1_out), .Q(Cause_q), .clk(clk));  // open: clr
  Multiplexer #(.width(16)) multiplexer_6 (
    .in0({16{1'b0}}), .in1(16'h4000), .out(multiplexer_6_out), .sel(or_2_out));  // open: en
  Multiplexer #(.select(2), .width(16)) multiplexer_7 (
    .in1(Cause_q), .in2(EPC_q), .in3(16'h6666), .out(cp0_reg_value), .sel(bit_extender_1_out));  // open: in0, en
  Multiplexer #(.width(16)) multiplexer_8 (.in0(multiplexer_6_out), .in1(EPC_q), .out(cp0_pc), .sel(eret));  // open: en
endmodule

module CTRL (
  input  [4:0] in_1,
  output [2:0] npc_sel,
  output [3:0] alu_op,
  output mem_write,
  output reg_write,
  output eret,
  output mfc0,
  output mtc0
);

  wire add, addi, bdown, bup, cpfimm, cpfmem, jump, jumpneg, jumpz, not_1_out, not_2_out, not_3_out,
       not_4_out, not_5_out, sub, subi;

  not not_1 (not_1_out, in_1[4]);
  not not_2 (not_2_out, in_1[2]);
  not not_3 (not_3_out, in_1[3]);
  or or_1 (npc_sel[1], jumpz, jumpneg);
  or or_2 (npc_sel[0], jumpneg, jump);
  not not_4 (not_4_out, in_1[0]);
  not not_5 (not_5_out, in_1[1]);
  or or_3 (alu_op[2], cpfimm, cpfmem, bdown, bup);
  or or_4 (alu_op[1], cpfimm, cpfmem, subi, addi);
  or or_5 (alu_op[0], cpfimm, bdown, subi, sub);
  and u_addi (addi, not_1_out, not_3_out, not_2_out, in_1[1], not_4_out);
  and u_add (add, not_1_out, not_3_out, not_2_out, in_1[1], in_1[0]);
  and u_bup (bup, not_1_out, not_3_out, in_1[2], not_5_out, not_4_out);
  and u_bdown (bdown, not_1_out, not_3_out, in_1[2], in_1[1], not_4_out);
  and u_cpfimm (cpfimm, not_1_out, in_1[3], not_2_out, not_5_out, not_4_out);
  and u_cpfmem (cpfmem, not_1_out, in_1[3], not_2_out, not_5_out, in_1[0]);
  and cpt (mem_write, not_1_out, in_1[3], not_2_out, in_1[1], not_4_out);
  and u_eret (eret, in_1[4], in_1[3], in_1[2], in_1[1], in_1[0]);
  and u_jump (jump, not_1_out, in_1[3], in_1[2], not_5_out, not_4_out);
  and u_jumpneg (jumpneg, not_1_out, in_1[3], in_1[2], in_1[1], not_4_out);
  and u_jumpz (jumpz, in_1[4], not_3_out, not_2_out, not_5_out, not_4_out);
  and u_mfc0 (mfc0, in_1[4], in_1[3], in_1[2], not_5_out, not_4_out);
  and u_mtc0 (mtc0, in_1[4], in_1[3], in_1[2], not_5_out, in_1[0]);
  and u_subi (subi, in_1[4], not_3_out, not_2_out, in_1[1], not_4_out);
  and u_sub (sub, in_1[4], not_3_out, not_2_out, in_1[1], in_1[0]);
  or or_6 (reg_write, mfc0, cpfimm, cpfmem, bdown, bup, subi, addi, sub, add);

  assign alu_op[3] = 1'b0;
  assign npc_sel[2] = 1'b0;

  // Other names for the same wires on the sheet: cpt = mem_write
endmodule
